# Fritzing sketch counter (saved by Fritzing 0.7.5b)
breadboards: 1

parts:
  Arduino1 = Arduino
  R1 = Resistor [tolerance=±5% resistance=220 package=THT]
  R2 = Resistor [tolerance=±5% resistance=220 package=THT]
  R3 = Resistor [tolerance=±5% resistance=220 package=THT]
  LED2 = LED - 3mm [color="Green (565nm)" package="3 mm [THT]"]
  LED3 = LED - 3mm [color="Yellow (595nm)" package="3 mm [THT]"]
  LED1 = LED - 3mm [color="Red (633nm)" package="3 mm [THT]"]
  J3 = single row smd male pin header, 6 pins [form="♂ (male)"]
  K1 = Relay [part_number=FRS1B-S package=THT]
  J4 = screw terminal, 2 pins
  M1 = DC Motor
  U1 = mystery part, 5 pins [chip_label=HEDS-9140 spacing=300mil]
  J5 = single row smd male pin header, 6 pins [form="♂ (male)"]
  J2 = single row smd male pin header, 5 pins [form="♂ (male)"]
  S1 = Pushbutton [package="[THT]"]
  R4 = Resistor [tolerance=±5% resistance=220 package=THT]

nets (from the schematic view):
  N1: Arduino1.GND, R1.Pin_0, J3.pin1, K1.COIL1, J2.pin1
  N2: Arduino1.D13, LED1.anode
  N3: Arduino1.D7, S1.Pin_3, S1.Pin_4, R4.Pin_1
  N4: Arduino1.D6, LED3.anode
  N5: Arduino1.D5, LED2.anode, K1.COIL2
  N6: Arduino1.D4, J3.pin5, J2.pin5
  N7: Arduino1.D3, J3.pin3, J2.pin3
  N8: Arduino1.D2, J3.pin2, J2.pin2
  N9: Arduino1.+5V, J3.pin4, J2.pin4, S1.Pin_1, S1.Pin_2
  N10: R2.Pin_0, R3.Pin_0, R4.Pin_0
  N11: J3.pin6, J5.pin6
  N12: K1.C1, J4.pin1
  N13: K1.B, M1.pin_2
  N14: J4.pin2, M1.pin_1
  N15: U1.pin1, J5.pin5
  N16: U1.pin2, J5.pin4
  N17: U1.pin3, J5.pin3
  N18: U1.pin4, J5.pin2
  N19: U1.pin5, J5.pin1

notes:
  AC Motor
  Encoder
  AC power
